# Fritzing sketch test Sketch (fritz) (saved by Fritzing 0.9.3b)
breadboards: 1

parts:
  Part1 = Arduino Uno (Rev3)
  FC-1 = Sound Sensor

nets:
  N1: Part1.A0, FC-1.OUT
  5V: Part1.5V, FC-1.VCC
  GND: Part1.GND, FC-1.GND

// code stored in the sketch: Untitled2.ino
const int OUT_PIN = 8;
const int SAMPLE_TIME = 10;
unsigned long millisCurrent;
unsigned long millisLast = 0;
unsigned long millisElapsed = 0;
int sampleBufferValue = 0;
void setup()
 { 
  Serial.begin(9600);
}
void loop() {
 
  millisCurrent = millis();
   millisElapsed = millisCurrent - millisLast;
 
   if (digitalRead(OUT_PIN) == LOW) {
     sampleBufferValue++;
   }
 
   if (millisElapsed > SAMPLE_TIME) {
    Serial.println(sampleBufferValue);
     sampleBufferValue = 0;
     millisLast = millisCurrent;
   }
 
 }
